// Logisim project core.circ as structural Verilog: 14 circuits, main circuit main
module register (
  input  [15:0] data_in,
  input  clk,
  input  write_enable,
  input  reset,
  output [15:0] data_out
);

  wire and_1_out;

  and and_1 (and_1_out, clk, write_enable);
  D_Flip_Flop d_ff_1 (.D(data_in[0]), .clk(and_1_out), .Q(data_out[0]), .reset(reset));  // open: Qn, preset
  D_Flip_Flop d_ff_2 (.D(data_in[1]), .clk(and_1_out), .Q(data_out[1]), .reset(reset));  // open: Qn, preset
  D_Flip_Flop d_ff_3 (.D(data_in[2]), .clk(and_1_out), .Q(data_out[2]), .reset(reset));  // open: Qn, preset
  D_Flip_Flop d_ff_4 (.D(data_in[3]), .clk(and_1_out), .Q(data_out[3]), .reset(reset));  // open: Qn, preset
  D_Flip_Flop d_ff_5 (.D(data_in[4]), .clk(and_1_out), .Q(data_out[4]), .reset(reset));  // open: Qn, preset
  D_Flip_Flop d_ff_6 (.D(data_in[5]), .clk(and_1_out), .Q(data_out[5]), .reset(reset));  // open: Qn, preset
  D_Flip_Flop d_ff_7 (.D(data_in[6]), .clk(and_1_out), .Q(data_out[6]), .reset(reset));  // open: Qn, preset
  D_Flip_Flop d_ff_8 (.D(data_in[7]), .clk(and_1_out), .Q(data_out[7]), .reset(reset));  // open: Qn, preset
  D_Flip_Flop d_ff_9 (.D(data_in[8]), .clk(and_1_out), .Q(data_out[8]), .reset(reset));  // open: Qn, preset
  D_Flip_Flop d_ff_10 (.D(data_in[9]), .clk(and_1_out), .Q(data_out[9]), .reset(reset));  // open: Qn, preset
  D_Flip_Flop d_ff_11 (.D(data_in[10]), .clk(and_1_out), .Q(data_out[10]), .reset(reset));  // open: Qn, preset
  D_Flip_Flop d_ff_12 (.D(data_in[11]), .clk(and_1_out), .Q(data_out[11]), .reset(reset));  // open: Qn, preset
  D_Flip_Flop d_ff_13 (.D(data_in[12]), .clk(and_1_out), .Q(data_out[12]), .reset(reset));  // open: Qn, preset
  D_Flip_Flop d_ff_14 (.D(data_in[13]), .clk(and_1_out), .Q(data_out[13]), .reset(reset));  // open: Qn, preset
  D_Flip_Flop d_ff_15 (.D(data_in[14]), .clk(and_1_out), .Q(data_out[14]), .reset(reset));  // open: Qn, preset
  D_Flip_Flop d_ff_16 (.D(data_in[15]), .clk(and_1_out), .Q(data_out[15]), .reset(reset));  // open: Qn, preset

  // Other names for the same wires on the sheet: outconnect[15:0] = data_out
endmodule

module RegisterFile (
  input  [2:0] rd,
  input  [15:0] data_in,
  input  in_3,
  input  reset,
  input  write_enable,
  input  [2:0] rs1,
  input  [2:0] rs2,
  output [15:0] rs1_contents,
  output [15:0] rs2_contents
);

  wire decoder_1_out1, decoder_1_out2, decoder_1_out3, decoder_1_out4, decoder_1_out5, decoder_1_out6,
       decoder_1_out7;
  wire [15:0] register_1_data_out, register_2_data_out, register_3_data_out, register_4_data_out,
       register_5_data_out, register_6_data_out, register_7_data_out;

  // Probe on register_4_data_out
  // Probe on register_2_data_out
  // Probe on register_5_data_out
  // Probe on register_6_data_out
  Decoder #(.select(3)) decoder_1 (
    .out1(decoder_1_out1), .out2(decoder_1_out2), .out3(decoder_1_out3), .out4(decoder_1_out4),
    .out5(decoder_1_out5), .out6(decoder_1_out6), .out7(decoder_1_out7), .sel(rd), .en(write_enable));  // open: out0
  // Probe on register_7_data_out
  // Probe on register_3_data_out
  register register_1 (
    .data_in(data_in), .clk(in_3), .write_enable(decoder_1_out1), .reset(reset),
    .data_out(register_1_data_out));
  register register_2 (
    .data_in(data_in), .clk(in_3), .write_enable(decoder_1_out2), .reset(reset),
    .data_out(register_2_data_out));
  register register_3 (
    .data_in(data_in), .clk(in_3), .write_enable(decoder_1_out3), .reset(reset),
    .data_out(register_3_data_out));
  register register_4 (
    .data_in(data_in), .clk(in_3), .write_enable(decoder_1_out4), .reset(reset),
    .data_out(register_4_data_out));
  register register_5 (
    .data_in(data_in), .clk(in_3), .write_enable(decoder_1_out5), .reset(reset),
    .data_out(register_5_data_out));
  register register_6 (
    .data_in(data_in), .clk(in_3), .write_enable(decoder_1_out6), .reset(reset),
    .data_out(register_6_data_out));
  register register_7 (
    .data_in(data_in), .clk(in_3), .write_enable(decoder_1_out7), .reset(reset),
    .data_out(register_7_data_out));
  // Probe on register_1_data_out
  // Probe on {16{1'b0}}
  Multiplexer #(.select(3), .width(16), .enable("false")) multiplexer_1 (
    .in0({16{1'b0}}), .in1(register_1_data_out), .in2(register_2_data_out), .in3(register_3_data_out),
    .in4(register_4_data_out), .in5(register_5_data_out), .in6(register_6_data_out),
    .in7(register_7_data_out), .out(rs1_contents), .sel(rs1));
  Multiplexer #(.select(3), .width(16), .enable("false")) multiplexer_2 (
    .in0({16{1'b0}}), .in1(register_1_data_out), .in2(register_2_data_out), .in3(register_3_data_out),
    .in4(register_4_data_out), .in5(register_5_data_out), .in6(register_6_data_out),
    .in7(register_7_data_out), .out(rs2_contents), .sel(rs2));
endmodule

module alu (
  input  [15:0] A,
  input  [15:0] B,
  input  [1:0] select,
  output [15:0] data_out
);

  wire [15:0] adder_1_output, adder_2_output, not_1_out, or_1_out;

  adder adder_1 (.sub(1'b0), .\output (adder_1_output), .A(A), .B(B));  // open: ovf
  adder adder_2 (.sub(1'b1), .\output (adder_2_output), .A(A), .B(B));  // open: ovf
  assign not_1_out = ~A;  // NOT_Gate not_1, 16 bits wide
  assign or_1_out = A | B;  // OR_Gate or_1, 16 bits wide
  Multiplexer #(.select(2), .width(16), .enable("false")) multiplexer_1 (
    .in0(adder_1_output), .in1(adder_2_output), .in2(or_1_out), .in3(not_1_out), .out(data_out), .sel(select));
endmodule

module add (
  input  in_1,
  input  in_2,
  input  in_3,
  input  in_4,
  output out_5,
  output out_6
);

  wire and_1_out, and_2_out, xor_1_out, xor_2_out;

  xor xor_1 (xor_1_out, in_3, in_4);
  and and_1 (and_1_out, xor_1_out, in_2);
  xor xor_2 (xor_2_out, in_2, xor_1_out);
  or or_1 (out_6, and_1_out, and_2_out);
  and and_2 (and_2_out, xor_2_out, in_1);
  xor xor_3 (out_5, in_1, xor_2_out);
endmodule

module adder (
  input  sub,
  input  [15:0] A,
  input  [15:0] B,
  output [15:0] \output ,
  output ovf
);

  wire add_1_out_6, add_2_out_6, add_3_out_6, add_4_out_6, add_5_out_6, add_6_out_6, add_7_out_6,
       add_8_out_6, add_9_out_6, add_10_out_6, add_11_out_6, add_12_out_6, add_13_out_6, add_14_out_6,
       add_15_out_6, add_16_out_6;

  add add_1 (.in_2(A[0]), .in_3(sub), .in_4(B[0]), .in_1(sub), .out_6(add_1_out_6), .out_5(\output [0]));
  add add_2 (.in_2(A[1]), .in_3(sub), .in_4(B[1]), .in_1(add_1_out_6), .out_6(add_2_out_6), .out_5(\output [1]));
  add add_3 (.in_2(A[2]), .in_3(sub), .in_4(B[2]), .in_1(add_2_out_6), .out_6(add_3_out_6), .out_5(\output [2]));
  add add_4 (.in_2(A[3]), .in_3(sub), .in_4(B[3]), .in_1(add_3_out_6), .out_6(add_4_out_6), .out_5(\output [3]));
  add add_5 (.in_2(A[4]), .in_3(sub), .in_4(B[4]), .in_1(add_4_out_6), .out_6(add_5_out_6), .out_5(\output [4]));
  add add_6 (.in_2(A[5]), .in_3(sub), .in_4(B[5]), .in_1(add_5_out_6), .out_6(add_6_out_6), .out_5(\output [5]));
  add add_7 (.in_2(A[6]), .in_3(sub), .in_4(B[6]), .in_1(add_6_out_6), .out_6(add_7_out_6), .out_5(\output [6]));
  add add_8 (.in_2(A[7]), .in_3(sub), .in_4(B[7]), .in_1(add_7_out_6), .out_6(add_8_out_6), .out_5(\output [7]));
  add add_9 (.in_2(A[8]), .in_3(sub), .in_4(B[8]), .in_1(add_8_out_6), .out_6(add_9_out_6), .out_5(\output [8]));
  add add_10 (.in_2(A[9]), .in_3(sub), .in_4(B[9]), .in_1(add_9_out_6), .out_6(add_10_out_6), .out_5(\output [9]));
  add add_11 (.in_2(A[10]), .in_3(sub), .in_4(B[10]), .in_1(add_10_out_6), .out_6(add_11_out_6), .out_5(\output [10]));
  add add_12 (.in_2(A[11]), .in_3(sub), .in_4(B[11]), .in_1(add_11_out_6), .out_6(add_12_out_6), .out_5(\output [11]));
  add add_13 (.in_2(A[12]), .in_3(sub), .in_4(B[12]), .in_1(add_12_out_6), .out_6(add_13_out_6), .out_5(\output [12]));
  add add_14 (.in_2(A[13]), .in_3(sub), .in_4(B[13]), .in_1(add_13_out_6), .out_6(add_14_out_6), .out_5(\output [13]));
  add add_15 (.in_2(A[14]), .in_3(sub), .in_4(B[14]), .in_1(add_14_out_6), .out_6(add_15_out_6), .out_5(\output [14]));
  add add_16 (.in_2(A[15]), .in_3(sub), .in_4(B[15]), .in_1(add_15_out_6), .out_6(add_16_out_6), .out_5(\output [15]));
  xor xor_1 (ovf, add_16_out_6, add_15_out_6);
endmodule

module main (
  input  [1:0] in_1,
  input  reset
);

  wire \and , and_2_out, bgt, branch, clock_1_out, gout_1_out, hi, in, iRt, iRtAlu, j, jal, jr,
       keyboard_1_avail, lw1, memorylatch_1_oe_latched, memorylatch_1_we_latched, multiplexer_10_out,
       not_1_out, \or , sw, we, zout_1_out;
  wire [0:0] control1_1_subtract;
  wire [2:0] multiplexer_5_out, multiplexer_6_out;
  wire [6:0] keyboard_1_data, registerfile_1_rs1_contents;
  wire [7:7] not_2_out;
  wire [11:0] rom_1_data;
  wire [15:0] alu_1_data_out, alu_2_data_out, alu_3_data_out, and_1_out, bit_extender_1_out,
       bit_extender_2_out, memorylatch_1_address_latched, memorylatch_1_data_in_latched, multiplexer_1_out,
       multiplexer_2_out, multiplexer_3_out, multiplexer_4_out, multiplexer_7_out, multiplexer_8_out,
       multiplexer_9_out, multiplexer_11_out, multiplexer_12_out, or_1_out, ram_1_dout, register_1_data_out,
       registerfile_1_rs2_contents;
  wire [15:7] registerfile_1_rs1_contents_2;
  wire [15:12] rom_1_data_2;

  Clock clock_1 (.out(clock_1_out));
  TTY #(.rows(13), .cols(80), .trigger("falling")) tty_1 (
    .data(registerfile_1_rs1_contents), .clk(clock_1_out), .we(hi), .clr(reset));
  not not_1 (not_1_out, clock_1_out);
  register register_1 (
    .data_in(multiplexer_1_out), .clk(clock_1_out), .write_enable(1'b1), .reset(reset),
    .data_out(register_1_data_out));
  alu alu_1 (.A(register_1_data_out), .B(16'h1), .select(2'b00), .data_out(alu_1_data_out));
  ROM #(.addrWidth(16), .dataWidth(16)) rom_1 (.addr(register_1_data_out), .data({rom_1_data_2, rom_1_data}));
  Multiplexer #(.width(16), .enable("false")) multiplexer_1 (
    .in0(multiplexer_9_out), .in1({registerfile_1_rs1_contents_2, registerfile_1_rs1_contents}),
    .out(multiplexer_1_out), .sel(jr));
  Multiplexer #(.width(16), .enable("false")) multiplexer_2 (
    .in0(multiplexer_3_out), .in1(bit_extender_2_out), .out(multiplexer_2_out), .sel(in));
  Multiplexer #(.width(16), .enable("false")) multiplexer_3 (
    .in0(multiplexer_4_out), .in1(alu_1_data_out), .out(multiplexer_3_out), .sel(jal));
  Multiplexer #(.width(16), .enable("false")) multiplexer_4 (
    .in0(multiplexer_7_out), .in1(and_1_out), .out(multiplexer_4_out), .sel(\and ));
  Multiplexer #(.width(3), .enable("false")) multiplexer_5 (
    .in0(multiplexer_6_out), .in1(3'b111), .out(multiplexer_5_out), .sel(jal));
  Multiplexer #(.width(3), .enable("false")) multiplexer_6 (
    .in0(rom_1_data[5:3]), .in1(rom_1_data[8:6]), .out(multiplexer_6_out), .sel(iRt));
  assign and_1_out = {registerfile_1_rs1_contents_2, registerfile_1_rs1_contents} & registerfile_1_rs2_contents;  // AND_Gate and_1, 16 bits wide
  Multiplexer #(.width(16), .enable("false")) multiplexer_7 (
    .in0(multiplexer_12_out), .in1(or_1_out), .out(multiplexer_7_out), .sel(\or ));
  assign bit_extender_1_out = {{10{rom_1_data[5]}}, rom_1_data[5:0]};  // Bit_Extender bit_extender_1
  alu alu_2 (.A(alu_1_data_out), .B(bit_extender_1_out), .select(in_1), .data_out(alu_2_data_out));
  assign or_1_out = {registerfile_1_rs1_contents_2, registerfile_1_rs1_contents} | registerfile_1_rs2_contents;  // OR_Gate or_1, 16 bits wide
  RegisterFile registerfile_1 (
    .rd(multiplexer_5_out), .data_in(multiplexer_2_out), .in_3(not_1_out), .reset(reset), .write_enable(we),
    .rs1(rom_1_data[11:9]), .rs2(rom_1_data[8:6]),
    .rs1_contents({registerfile_1_rs1_contents_2, registerfile_1_rs1_contents}),
    .rs2_contents(registerfile_1_rs2_contents));
  Multiplexer #(.width(16), .enable("false")) multiplexer_8 (
    .in0(registerfile_1_rs2_contents), .in1(bit_extender_1_out), .out(multiplexer_8_out), .sel(iRtAlu));
  Multiplexer #(.width(16), .enable("false")) multiplexer_9 (
    .in0(multiplexer_11_out), .in1({alu_1_data_out[15:12], rom_1_data}), .out(multiplexer_9_out), .sel(j));
  Multiplexer #(.enable("false")) multiplexer_10 (
    .in0(zout_1_out), .in1(gout_1_out), .out(multiplexer_10_out), .sel(bgt));
  gout gout_1 (.in(alu_3_data_out), .out(gout_1_out));
  zOut zout_1 (.in(alu_3_data_out), .out(zout_1_out));
  alu alu_3 (
    .A({registerfile_1_rs1_contents_2, registerfile_1_rs1_contents}), .B(multiplexer_8_out),
    .select({1'b0, control1_1_subtract[0]}), .data_out(alu_3_data_out));
  control1 control1_1 (
    .in_1(rom_1_data_2), .\or (\or ), .\and (\and ), .iRt(iRt), .iRtAlu(iRtAlu),
    .subtract(control1_1_subtract[0]), .lw1(lw1), .sw(sw), .we(we), .branch(branch), .bgt(bgt), .j(j),
    .jal(jal), .jr(jr), .hi(hi), .in(in));
  RAM #(.addrWidth(16), .dataWidth(16), .trigger("high"), .databus("bibus")) ram_1 (
    .addr(memorylatch_1_address_latched), .we(memorylatch_1_we_latched), .oe(memorylatch_1_oe_latched),
    .din(memorylatch_1_data_in_latched), .dout(ram_1_dout));
  memorylatch memorylatch_1 (
    .address(alu_3_data_out), .WE(sw), .clk(clock_1_out), .data_in(registerfile_1_rs2_contents),
    .address_latched(memorylatch_1_address_latched), .WE_latched(memorylatch_1_we_latched),
    .OE_latched(memorylatch_1_oe_latched), .data_in_latched(memorylatch_1_data_in_latched));
  Keyboard keyboard_1 (.clk(clock_1_out), .re(in), .clr(reset), .avail(keyboard_1_avail), .data(keyboard_1_data));
  Multiplexer #(.width(16), .enable("false")) multiplexer_11 (
    .in0(alu_1_data_out), .in1(alu_2_data_out), .out(multiplexer_11_out), .sel(and_2_out));
  and and_2 (and_2_out, branch, multiplexer_10_out);
  Multiplexer #(.width(16), .enable("false")) multiplexer_12 (
    .in0(alu_3_data_out), .in1(ram_1_dout), .out(multiplexer_12_out), .sel(lw1));
  not not_2 (not_2_out[7], keyboard_1_avail);
  assign bit_extender_2_out = {{8{1'b0}}, {not_2_out[7], keyboard_1_data}};  // Bit_Extender bit_extender_2
endmodule

module control1 (
  input  [3:0] in_1,
  output \or ,
  output \and ,
  output iRt,
  output iRtAlu,
  output subtract,
  output lw1,
  output sw,
  output we,
  output branch,
  output bgt,
  output j,
  output jal,
  output jr,
  output hi,
  output in
);

  wire decoder_1_out4, decoder_1_out8, decoder_1_out10, decoder_1_out13, not_1_out, not_2_out, not_3_out,
       not_4_out, not_5_out, not_6_out;

  Decoder #(.select(4)) decoder_1 (
    .out0(hi), .out1(in), .out2(lw1), .out3(sw), .out4(decoder_1_out4), .out5(bgt), .out6(\or ),
    .out7(\and ), .out8(decoder_1_out8), .out10(decoder_1_out10), .out13(decoder_1_out13), .out14(jal),
    .out15(jr), .sel(in_1));  // open: out9, out11, out12, en
  or or_1 (subtract, decoder_1_out10, bgt, decoder_1_out4);
  not not_1 (not_1_out, bgt);
  not not_2 (not_2_out, decoder_1_out13);
  not not_3 (not_3_out, hi);
  not not_4 (not_4_out, sw);
  not not_5 (not_5_out, decoder_1_out4);
  not not_6 (not_6_out, jr);
  or or_2 (iRt, decoder_1_out8, sw, lw1);
  or or_3 (iRtAlu, decoder_1_out8, sw, lw1);
  and and_1 (we, not_4_out, not_1_out, not_6_out, not_2_out, not_5_out, not_3_out);
  or or_4 (branch, decoder_1_out4, bgt);
  or or_5 (j, decoder_1_out13, jal);
endmodule

module zOut (
  input  [15:0] in,
  output out
);

  nor nor_1 (out, in[0], in[1], in[2], in[3], in[4], in[5], in[6], in[7], in[9], in[10], in[11], in[12], in[13], in[14], in[15]);
endmodule

module gout (
  input  [15:0] in,
  output out
);

  wire nor_1_out, not_1_out, not_2_out;

  nor nor_1 (nor_1_out, in[0], in[1], in[2], in[3], in[4], in[5], in[6], in[7], in[8], in[9], in[10], in[11], in[12], in[13], in[14]);
  not not_1 (not_1_out, nor_1_out);
  not not_2 (not_2_out, in[15]);
  and and_1 (out, not_1_out, not_2_out);
endmodule

module memorylatch (
  input  [15:0] address,
  input  WE,
  input  clk,
  input  [15:0] data_in,
  output [15:0] address_latched,
  output WE_latched,
  output OE_latched,
  output [15:0] data_in_latched
);

  wire d_ff_1_q;
  wire [15:0] register_1_q;

  Register #(.width(16), .trigger("falling")) register_1 (
    .D(address), .en(WE), .clk(clk), .Q(register_1_q));  // open: clr
  D_Flip_Flop #(.trigger("falling")) d_ff_1 (.D(WE), .clk(clk), .Q(d_ff_1_q));  // open: Qn, preset, reset
  Register #(.width(16), .trigger("falling")) register_2 (
    .D(data_in), .en(WE), .clk(clk), .Q(data_in_latched));  // open: clr
  Multiplexer #(.width(16), .enable("false")) multiplexer_1 (
    .in0(address), .in1(register_1_q), .out(address_latched), .sel(d_ff_1_q));
  and and_1 (WE_latched, clk, d_ff_1_q);
  not not_1 (OE_latched, WE_latched);
endmodule

module shifter (
  input  in16,
  input  in15,
  input  in14,
  input  in13,
  input  in12,
  input  in11,
  input  in10,
  input  in9,
  input  in8,
  input  in7,
  input  in6,
  input  in5,
  input  in4,
  input  in3,
  input  in2,
  input  in1,
  output o15,
  output o14,
  output o13,
  output o12,
  output o11,
  output o10,
  output o9,
  output o8,
  output o7,
  output o6,
  output o5,
  output o4,
  output o3,
  output o2,
  output o1
);

  Multiplexer #(.enable("false")) multiplexer_1 (.in0(in16), .in1(in15), .out(o15));  // open: sel
  Multiplexer #(.enable("false")) multiplexer_2 (.in0(in3), .in1(in2), .out(o2));  // open: sel
  Multiplexer #(.enable("false")) multiplexer_3 (.in0(in15), .in1(in14), .out(o14));  // open: sel
  Multiplexer #(.enable("false")) multiplexer_4 (.in0(in14), .in1(in13), .out(o13));  // open: sel
  Multiplexer #(.enable("false")) multiplexer_5 (.in0(in13), .in1(in12), .out(o12));  // open: sel
  Multiplexer #(.enable("false")) multiplexer_6 (.in0(in11), .in1(in10), .out(o10));  // open: sel
  Multiplexer #(.enable("false")) multiplexer_7 (.in0(in10), .in1(in9), .out(o9));  // open: sel
  Multiplexer #(.enable("false")) multiplexer_8 (.in0(in5), .in1(in4), .out(o4));  // open: sel
  Multiplexer #(.enable("false")) multiplexer_9 (.in0(in4), .in1(in3), .out(o3));  // open: sel
  Multiplexer #(.enable("false")) multiplexer_10 (.in0(in2), .in1(in1), .out(o1));  // open: sel
  Multiplexer #(.enable("false")) multiplexer_11 (.in0(in12), .in1(in11), .out(o11));  // open: sel
  Multiplexer #(.enable("false")) multiplexer_12 (.in0(in9), .in1(in8), .out(o8));  // open: sel
  Multiplexer #(.enable("false")) multiplexer_13 (.in0(in8), .in1(in7), .out(o7));  // open: sel
  Multiplexer #(.enable("false")) multiplexer_14 (.in0(in7), .in1(in6), .out(o6));  // open: sel
  Multiplexer #(.enable("false")) multiplexer_15 (.in0(in6), .in1(in5), .out(o5));  // open: sel
endmodule

module bit2shift (
  input  [15:0] in_1,
  output [13:0] out_2
);


  assign out_2 = in_1[15:2];
endmodule

module bit4shift (
  input  [15:0] in_1,
  output [11:0] out_2
);


  assign out_2 = in_1[15:4];
endmodule

module bit1shift (
  input  [15:0] in_1,
  output [14:0] out_2
);


  assign out_2 = in_1[15:1];
endmodule
